# Fritzing sketch ESP32-CAM-Breadboard (saved by Fritzing 0.9.3b)
circuit board: 5.89309cm x 5.5557cm
breadboards: 1

parts:
  S1 = Momentary Switch [package=tactile-pth]
  S2 = Momentary Switch [package=tactile-pth]
  X1 = USB Connectors [package=usb-microb]
  Part1 = FTDI Basic Programmer
  Mod1 = ESP32 - CAM

nets:
  N1: S1.2, Mod1.IO12
  GND: S1.3, S2.3, X1.GND, Part1.GND, Mod1.GND
  N2: S2.2, Mod1.IO0
  N3: X1.VBUS, Mod1.5V
  N4: Part1.RXI, Mod1.VOT
  N5: Part1.TXO, Mod1.VOR

notes:
  Upload button
  OTA button
  5V supply
  USB micro
  FTDI Serial to USB
  for programming

custom parts:
  ESP32 - CAM: The ESP32-CAM has a very competitive small-size camera module that can operate independently as a minimum system with a footprint of only 27*40.5*4.5mm and a deep sleep current of up to 6mA.
